# Fritzing sketch MusicInstrumentButtonMachine (saved by Fritzing 0.9.3b)
breadboards: 1

parts:
  Parts1 = SparkFun RedBoard [part_number=DEV-12757]
  S4 = Pushbutton [package="[THT]"]
  S6 = Pushbutton [package="[THT]"]
  S7 = Pushbutton [package="[THT]"]
  S8 = Pushbutton [package="[THT]"]
  S9 = Pushbutton [package="[THT]"]

nets:
  N1: Parts1.D8, S4.Pin_1, S4.Pin_2
  N2: Parts1.D9_PWM, S6.Pin_1, S6.Pin_2
  N3: Parts1.GND, Parts1.D6_PWM, S4.Pin_3, S4.Pin_4, S6.Pin_3, S6.Pin_4, S7.Pin_3, S7.Pin_4, S8.Pin_3, S8.Pin_4, S9.Pin_3, S9.Pin_4
  N4: Parts1.D5_PWM, S9.Pin_1, S9.Pin_2
  N5: Parts1.D7, S7.Pin_1, S7.Pin_2
  N6: S8.Pin_1, S8.Pin_2

custom parts:
  SparkFun RedBoard: At SparkFun we use many Arduinos and we’re always looking for the simplest, most stable one. Each board is a bit different and no one board has everything we want, so we decided to make our own version that combines all our favorite features. The RedBoard combines the simplicity of the UNO’s Optiboot bootloader (which is used in the Pro series), the stability of the FTDI (which we all missed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
  Pushbutton: A generic pushbutton.
  Pushbutton: A generic pushbutton.
  Pushbutton: A generic pushbutton.
  Pushbutton: A generic pushbutton.
